// Logisim project SymulatorProfesora.circ as structural Verilog: 1 circuit, main circuit main
module main (
  input  in_1,
  input  in_2,
  input  send,
  input  send_2,
  input  send_3,
  input  send_4,
  input  send_5,
  input  send_6
);

  wire clock_1_out, clock_2_out, clock_3_out, comparator_1_eq, comparator_2_eq, main_1_pulse, main_9_catch,
       main_10_catch, main_11_catch, main_12_catch, main_13_catch, main_14_catch, main_15_done, or_1_out,
       or_3_out;
  wire [4:0] adder_1_out, counter_1_q, counter_2_q, register_1_q;
  wire [6:0] keyboard_1_data, main_2_output;
  wire [15:0] score;
  wire [23:0] main_16_p3;
  wire [31:0] main_3_output, main_4_output, main_5_output, main_6_output, main_7_output, main_8_output,
       main_15_out_4, main_15_out_5, main_15_out_6, main_15_out_7, main_15_out_8, main_15_out_9,
       main_15_out_10, main_15_out_11, main_15_out_12, main_15_out_13, main_15_out_14, main_15_out_15,
       main_15_out_16, main_15_out_17, main_15_out_18, main_15_out_19, main_15_out_20, main_15_out_21,
       main_15_out_22, main_15_out_23, main_15_out_24, main_15_out_25, main_15_out_26, main_15_out_27,
       main_15_out_28, main_15_out_29, main_15_out_30, main_15_out_31, main_15_out_32, main_15_out_33,
       main_15_out_34, main_15_out_35, main_16_p4, or_2_out, rom_1_data, rom_2_data, rom_3_data, rom_4_data,
       rom_5_data, rom_6_data, rom_7_data;

  Keyboard #(.buflen(1)) keyboard_1 (.clk(clock_1_out), .re(1'b1), .data(keyboard_1_data));  // open: clr, avail
  Comparator #(.width(7), .mode("unsigned")) comparator_1 (
    .a(keyboard_1_data), .b(7'b1100100), .eq(comparator_1_eq));  // open: gt, lt
  Comparator #(.width(7), .mode("unsigned")) comparator_2 (
    .a(keyboard_1_data), .b(7'b1100001), .eq(comparator_2_eq));  // open: gt, lt
  Counter #(.width(5), .max('h1b), .ongoal("stay")) counter_1 (
    .load(comparator_1_eq), .Q(counter_1_q), .clk(or_1_out));  // open: D, count, carry, clr
  or or_1 (or_1_out, comparator_1_eq, comparator_2_eq);
  Counter #(.width(5), .max('h1f)) counter_2 (.Q(counter_2_q), .clk(clock_1_out));  // open: load, D, count, carry, clr
  Clock clock_1 (.out(clock_1_out));
  Register #(.width(5)) register_1 (.D(counter_1_q), .Q(register_1_q), .clk(main_15_done));  // open: en, clr
  Clock clock_2 (.out(clock_2_out));
  Adder #(.width(5)) adder_1 (.a(register_1_q), .b(counter_2_q), .out(adder_1_out));  // open: cin, cout
  comparator_score_thresholds_main main_1 (
    .score(score), .reset(in_1), .pulse(main_1_pulse), .clk(clock_2_out));  // open: out
  ROM #(.addrWidth(5), .dataWidth(32)) rom_1 (.addr(adder_1_out), .data(rom_1_data));  // open: sel
  ROM_message_spitter_main main_2 (.clock(clock_2_out), .\output (main_2_output), .trigger(main_1_pulse), .reset(in_2));
  ROM #(.addrWidth(5), .dataWidth(32)) rom_2 (.addr(counter_2_q), .data(rom_2_data));  // open: sel
  ROM #(.addrWidth(5), .dataWidth(32)) rom_3 (.addr(counter_2_q), .data(rom_3_data));  // open: sel
  ROM #(.addrWidth(5), .dataWidth(32)) rom_4 (.addr(counter_2_q), .data(rom_4_data));  // open: sel
  ROM #(.addrWidth(5), .dataWidth(32)) rom_5 (.addr(counter_2_q), .data(rom_5_data));  // open: sel
  ROM #(.addrWidth(5), .dataWidth(32)) rom_6 (.addr(counter_2_q), .data(rom_6_data));  // open: sel
  ROM #(.addrWidth(5), .dataWidth(32)) rom_7 (.addr(counter_2_q), .data(rom_7_data));  // open: sel
  Clock #(.highDuration(64), .lowDuration(64)) clock_3 (.out(clock_3_out));
  TTY #(.rows(1), .cols(110)) tty_1 (.data(main_2_output), .clk(clock_2_out), .clr(main_1_pulse));  // open: we
  student_drop_main main_3 (
    .\input (rom_2_data), .send(send), .\output (main_3_output), .catch(main_9_catch), .clk(clock_3_out));
  student_drop_main main_4 (
    .\input (rom_3_data), .send(send_2), .\output (main_4_output), .catch(main_10_catch), .clk(clock_3_out));
  student_drop_main main_5 (
    .\input (rom_4_data), .send(send_3), .\output (main_5_output), .catch(main_11_catch), .clk(clock_3_out));
  student_drop_main main_6 (
    .\input (rom_5_data), .send(send_4), .\output (main_6_output), .catch(main_12_catch), .clk(clock_3_out));
  student_drop_main main_7 (
    .\input (rom_6_data), .send(send_5), .\output (main_7_output), .catch(main_13_catch), .clk(clock_3_out));
  student_drop_main main_8 (
    .\input (rom_7_data), .send(send_6), .\output (main_8_output), .catch(main_14_catch), .clk(clock_3_out));
  student_catcher_main main_9 (.student(main_3_output), .catch(main_9_catch), .profesor(rom_1_data));
  student_catcher_main main_10 (.student(main_4_output), .catch(main_10_catch), .profesor(rom_1_data));
  student_catcher_main main_11 (.student(main_5_output), .catch(main_11_catch), .profesor(rom_1_data));
  student_catcher_main main_12 (.student(main_6_output), .catch(main_12_catch), .profesor(rom_1_data));
  student_catcher_main main_13 (.student(main_7_output), .catch(main_13_catch), .profesor(rom_1_data));
  student_catcher_main main_14 (.student(main_8_output), .catch(main_14_catch), .profesor(rom_1_data));
  assign or_2_out = main_3_output | main_4_output | main_5_output | rom_1_data | main_6_output | main_7_output | main_8_output;  // OR_Gate or_2, 32 bits wide
  or or_3 (or_3_out, main_14_catch, main_13_catch, main_12_catch, main_11_catch, main_10_catch, main_9_catch);
  display_buffer_main main_15 (
    .Address(or_2_out), .Select(counter_2_q), .out_4(main_15_out_4), .out_5(main_15_out_5),
    .out_6(main_15_out_6), .out_7(main_15_out_7), .out_8(main_15_out_8), .out_9(main_15_out_9),
    .out_10(main_15_out_10), .out_11(main_15_out_11), .out_12(main_15_out_12), .out_13(main_15_out_13),
    .out_14(main_15_out_14), .out_15(main_15_out_15), .out_16(main_15_out_16), .out_17(main_15_out_17),
    .out_18(main_15_out_18), .out_19(main_15_out_19), .out_20(main_15_out_20), .out_21(main_15_out_21),
    .out_22(main_15_out_22), .out_23(main_15_out_23), .out_24(main_15_out_24), .out_25(main_15_out_25),
    .out_26(main_15_out_26), .out_27(main_15_out_27), .out_28(main_15_out_28), .out_29(main_15_out_29),
    .out_30(main_15_out_30), .out_31(main_15_out_31), .out_32(main_15_out_32), .out_33(main_15_out_33),
    .out_34(main_15_out_34), .out_35(main_15_out_35), .Done(main_15_done));
  DotMatrix #(.matrixcols(32), .matrixrows(32)) dotmatrix_1 (
    .col0(main_15_out_4), .col1(main_15_out_5), .col2(main_15_out_6), .col3(main_15_out_7),
    .col4(main_15_out_8), .col5(main_15_out_9), .col6(main_15_out_10), .col7(main_15_out_11),
    .col8(main_15_out_12), .col9(main_15_out_13), .col10(main_15_out_14), .col11(main_15_out_15),
    .col12(main_15_out_16), .col13(main_15_out_17), .col14(main_15_out_18), .col15(main_15_out_19),
    .col16(main_15_out_20), .col17(main_15_out_21), .col18(main_15_out_22), .col19(main_15_out_23),
    .col20(main_15_out_24), .col21(main_15_out_25), .col22(main_15_out_26), .col23(main_15_out_27),
    .col24(main_15_out_28), .col25(main_15_out_29), .col26(main_15_out_30), .col27(main_15_out_31),
    .col28(main_15_out_32), .col29(main_15_out_33), .col30(main_15_out_34), .col31(main_15_out_35));
  // score_updater_main main_16: pin names not known; wires that end beside it: or_3_out, clock_1_out, main_16_p3, main_16_p4, score
  _7_Segment_Display u_7_segment_display_1 (
    .g(main_16_p3[17]), .f(main_16_p3[18]), .a(main_16_p3[23]), .b(main_16_p3[22]), .e(main_16_p3[19]),
    .d(main_16_p3[20]), .c(main_16_p3[21]), .dp(main_16_p3[16]));
  _7_Segment_Display u_7_segment_display_2 (
    .g(main_16_p4[25]), .f(main_16_p4[26]), .a(main_16_p4[31]), .b(main_16_p4[30]), .e(main_16_p4[27]),
    .d(main_16_p4[28]), .c(main_16_p4[29]), .dp(main_16_p4[24]));
  _7_Segment_Display u_7_segment_display_3 (
    .g(main_16_p3[9]), .f(main_16_p3[10]), .a(main_16_p3[15]), .b(main_16_p3[14]), .e(main_16_p3[11]),
    .d(main_16_p3[12]), .c(main_16_p3[13]), .dp(main_16_p3[8]));
  _7_Segment_Display u_7_segment_display_4 (
    .g(main_16_p4[17]), .f(main_16_p4[18]), .a(main_16_p4[23]), .b(main_16_p4[22]), .e(main_16_p4[19]),
    .d(main_16_p4[20]), .c(main_16_p4[21]), .dp(main_16_p4[16]));
  _7_Segment_Display u_7_segment_display_5 (
    .g(main_16_p3[1]), .f(main_16_p3[2]), .a(main_16_p3[7]), .b(main_16_p3[6]), .e(main_16_p3[3]),
    .d(main_16_p3[4]), .c(main_16_p3[5]), .dp(main_16_p3[0]));
  _7_Segment_Display u_7_segment_display_6 (
    .g(main_16_p4[9]), .f(main_16_p4[10]), .a(main_16_p4[15]), .b(main_16_p4[14]), .e(main_16_p4[11]),
    .d(main_16_p4[12]), .c(main_16_p4[13]), .dp(main_16_p4[8]));
  _7_Segment_Display u_7_segment_display_7 (
    .g(main_16_p4[1]), .f(main_16_p4[2]), .a(main_16_p4[7]), .b(main_16_p4[6]), .e(main_16_p4[3]),
    .d(main_16_p4[4]), .c(main_16_p4[5]), .dp(main_16_p4[0]));
  _7_Segment_Display u_7_segment_display_8 (
    .g(1'b0), .f(1'b1), .a(1'b1), .b(1'b1), .e(1'b1), .d(1'b1), .c(1'b1), .dp(1'b0));
  _7_Segment_Display u_7_segment_display_9 (
    .g(1'b0), .f(1'b1), .a(1'b1), .b(1'b1), .e(1'b1), .d(1'b1), .c(1'b1), .dp(1'b0));

  // Notes on the sheet:
  //   keyboard
  //   a
  //   d
  //   Zegar:szybko
  //   A6
  //   A5
  //   A4
  //   A3
  //   A2
  //   A1
  //   contents of rom_1 (hex, n*v repeats v):
  //   27*0 4 7 e 7 4
  //   profesor
  //   contents of rom_2 (hex, n*v repeats v):
  //   0 50000000 e0000000 50000000
  //   contents of rom_3 (hex, n*v repeats v):
  //   6*0 50000000 e0000000 50000000
  //   contents of rom_4 (hex, n*v repeats v):
  //   12*0 50000000 e0000000 50000000
  //   contents of rom_5 (hex, n*v repeats v):
  //   17*0 50000000 e0000000 50000000
  //   contents of rom_6 (hex, n*v repeats v):
  //   23*0 50000000 e0000000 50000000
  //   contents of rom_7 (hex, n*v repeats v):
  //   28*0 50000000 e0000000 50000000
  //   Skarbiec Profesora:
  //   zlapanych studentow
  //   PLN
endmodule
